# Fritzing sketch Circuit_Diagram (saved by Fritzing 0.9.3b)
breadboards: 1

parts:
  부품1 = Arduino Mega 2560 (Rev3)
  M1 = fc-51 [package=THT]
  YF-S201_Flow_Meter2 = YF-S201 Water Flow Meter
  VALVE1 = Plastic Solenoid Valve
  J2 = Power Jack [package=power_jack_smd]
  8_Channel_Relay1 = 8 Channel Power Relay
  M2 = fc-51 [package=THT]
  M3 = fc-51 [package=THT]
  M4 = fc-51 [package=THT]
  M5 = fc-51 [package=THT]
  YF-S201_Flow_Meter3 = YF-S201 Water Flow Meter
  YF-S201_Flow_Meter4 = YF-S201 Water Flow Meter
  YF-S201_Flow_Meter5 = YF-S201 Water Flow Meter
  YF-S201_Flow_Meter6 = YF-S201 Water Flow Meter
  VALVE2 = Plastic Solenoid Valve
  VALVE3 = Plastic Solenoid Valve
  VALVE4 = Plastic Solenoid Valve
  J3 = Power Jack [package=power_jack_smd]
  J4 = Power Jack [package=power_jack_smd]
  J5 = Power Jack [package=power_jack_smd]
  J6 = Power Jack [package=power_jack_smd]
  VALVE5 = Plastic Solenoid Valve
  M6 = DC Motor  # not connected
  M7 = DC Motor
  M8 = DC Motor
  M9 = DC Motor
  M10 = DC Motor

nets:
  N1: 부품1.D21/SCL, YF-S201_Flow_Meter2.SIG
  N2: 부품1.D20/SDA, YF-S201_Flow_Meter3.SIG
  N3: 부품1.D19/RX1, YF-S201_Flow_Meter4.SIG
  N4: 부품1.D18/TX1, YF-S201_Flow_Meter5.SIG
  N5: 부품1.D12_PWM, M1.pin1
  N6: 부품1.D11_PWM, M2.pin1
  N7: 부품1.D10_PWM, M3.pin1
  N8: 부품1.D9_PWM, M4.pin1
  N9: 부품1.D8_PWM, M5.pin1
  VCC: 부품1.5V, M1.pin3, YF-S201_Flow_Meter2.VCC, 8_Channel_Relay1.VCC, M2.pin3, M3.pin3, M4.pin3, M5.pin3, YF-S201_Flow_Meter3.VCC, YF-S201_Flow_Meter4.VCC, YF-S201_Flow_Meter5.VCC, YF-S201_Flow_Meter6.VCC
  GND: 부품1.GND, M1.pin2, YF-S201_Flow_Meter2.GND, 8_Channel_Relay1.GND, M2.pin2, M3.pin2, M4.pin2, M5.pin2, YF-S201_Flow_Meter3.GND, YF-S201_Flow_Meter4.GND, YF-S201_Flow_Meter5.GND, YF-S201_Flow_Meter6.GND
  N10: 부품1.D2_PWM, YF-S201_Flow_Meter6.SIG
  N11: 부품1.D3_PWM, 8_Channel_Relay1.IN1
  N12: 부품1.D4_PWM, 8_Channel_Relay1.IN2
  N13: 부품1.D5_PWM, 8_Channel_Relay1.IN3
  N14: 부품1.D6_PWM, 8_Channel_Relay1.IN4
  N15: 부품1.D7_PWM, 8_Channel_Relay1.IN5
  N16: VALVE1.no_name_yet#1, J2.GNDBREAK, M10.pin_2
  N17: VALVE1.no_name_yet#2, 8_Channel_Relay1.NO#23, M10.pin_1
  N18: J2.GND, 8_Channel_Relay1.COM#22
  N19: 8_Channel_Relay1.COM#25, J3.GND
  N20: 8_Channel_Relay1.NO#26, VALVE2.no_name_yet#2, M9.pin_1
  N21: 8_Channel_Relay1.COM#28, J4.GND
  N22: 8_Channel_Relay1.NO#29, VALVE3.no_name_yet#2, M8.pin_1
  N23: 8_Channel_Relay1.COM#31, J6.GND
  N24: 8_Channel_Relay1.NO#32, VALVE4.no_name_yet#2, M7.pin_1
  N25: 8_Channel_Relay1.COM#34, J5.GND
  N26: 8_Channel_Relay1.NO#35, VALVE5.no_name_yet#2
  N27: VALVE2.no_name_yet#1, J3.GNDBREAK
  N28: VALVE3.no_name_yet#1, J4.GNDBREAK, M8.pin_2
  N29: VALVE4.no_name_yet#1, J6.GNDBREAK, M7.pin_2
  N30: J5.GNDBREAK, VALVE5.no_name_yet#1

notes:
  FLOW_5
  FLOW_4
  FLOW_3
  FLOW_2
  FLOW_1
  PHOTO_1
  PHOTO_2
  PHOTO_3
  PHOTO_4
  PHOTO_5
  SOLENOID_1
  SOLENOID_2
  SOLENOID_3
  SOLENOID_4
  SOLENOID_5
  WATER_PUMP_1
  WATER_PUMP_2
  WATER_PUMP_3
  WATER_PUMP_4
  WATER_PUMP_5

custom parts:
  YF-S201 Water Flow Meter: The YF-S201 Flow Meter. The input voltage is 5V to 24V (DC).
  8 Channel Power Relay: An 8 channel power relay. The module operates at 5V.
